# Fritzing sketch AS3340_Test_2 (saved by Fritzing 0.9.5d)
breadboards: 1

parts:
  IC1 = IC, DIP package, 16 pins [chip_label=AS3340]
  R3 = Resistor [tolerance=±5% resistance=470 package=THT]
  C1 = Film/Foil Capacitor [capacitance=100nF voltage=35V package="5mm [THT, pp]"]
  R6 = Resistor [tolerance=±5% resistance=1.8k package=THT]
  R7 = Resistor [tolerance=±5% resistance=1.5M package=THT]
  C2 = Film/Foil Capacitor [capacitance=100nF voltage=35V package="5mm [THT, pp]"]
  R8 = Resistor [tolerance=±5% resistance=470 package=THT]
  C3 = Film/Foil Capacitor [capacitance=100nF voltage=35V package="5mm [THT, pp]"]
  R9 = Resistor [tolerance=±5% resistance=22k package=THT]
  R10 = TRIMPOT [package=trimpot_pth_s3_lock]
  R11 = Resistor [tolerance=±5% resistance=680 package=THT]
  R12 = Resistor [tolerance=±5% resistance=5.6k package=THT]
  R13 = Resistor [tolerance=±5% resistance=5.6k package=THT]
  C4 = Ceramic Capacitor [capacitance=100nF package="100 mil [THT, multilayer]"]
  C5 = Electrolytic Capacitor [capacitance=1µF package="100 mil [THT, electrolytic]"]
  C6 = Electrolytic Capacitor [capacitance=1µF package="100 mil [THT, electrolytic]"]
  R14 = TRIMPOT [package=trimpot_pth_s3_lock]
  C7 = Ceramic Capacitor [capacitance=100nF package="100 mil [THT, multilayer]"]
  R15 = Resistor [tolerance=±5% resistance=1M package=THT]
  R16 = Resistor [tolerance=±5% resistance=270k package=THT]
  C8 = Ceramic Capacitor [capacitance=100nF package="100 mil [THT, multilayer]"]
  R19 = Resistor [tolerance=±5% resistance=1M package=THT]
  C9 = Ceramic Capacitor [capacitance=100nF package="100 mil [THT, multilayer]"]
  R21 = TRIMPOT [package=trimpot_pth_s3_lock]
  R22 = Resistor [tolerance=±5% resistance=100k package=THT]
  R23 = Resistor [tolerance=±5% resistance=100k package=THT]
  R24 = Resistor [tolerance=±5% resistance=100k package=THT]

nets:
  N1: IC1.pin1, R9.Pin_1
  N2: IC1.pin2, R12.Pin_1
  N3: IC1.pin3, R10.CCW, R10.WIPER, R11.Pin_0, R12.Pin_0
  N4: IC1.pin4, IC1.pin8, R13.Pin_0
  N5: IC1.pin6, C7.0
  N6: IC1.pin7, R14.CW
  N7: IC1.pin9, C8.1
  N8: IC1.pin11, C2.+
  N9: IC1.pin12, C1.+, R6.Pin_0, C2.-, C3.-, R13.Pin_1, C4.1, C5.-, C6.+, R14.CCW
  N10: IC1.pin13, R7.Pin_1, R8.Pin_0, R19.Pin_0
  N11: IC1.pin14, R6.Pin_1
  N12: IC1.pin15, R3.Pin_1, R15.Pin_0, R16.Pin_1, R22.Pin_1, R23.Pin_1, R24.Pin_1
  N13: IC1.pin16, R7.Pin_0, C4.0, C5.+, R21.WIPER, R21.CW
  N14: R3.Pin_0, C1.-
  N15: R8.Pin_1, C3.+
  N16: R9.Pin_0, R10.CW
  N17: R11.Pin_1, C6.-
  N18: R14.WIPER, R15.Pin_1
  N19: R16.Pin_0, R21.CCW
  N20: R19.Pin_1, C9.0

notes:
  CVs
  Triangle 5V
  Pulse 12V
  Saw 10V
  GND
  +12V
  -12V
  GND
  PWM
  0-5V
  AS3340
  1 Scale1 16 VCC
  2 Scale2 15 VFCI
  3 VEE 14 Scale
  4 VP 13 VLFI
  5 VPWM 12 GND
  6 VHSI 11 Cap
  7 VHFT 10 VTO
  8 VSO 9 VSSI
  Hard
  Sync
  Soft Sync
  LIN FM
