# Fritzing sketch AS3340_Test_3 (saved by Fritzing 0.9.5d)
breadboards: 2

parts:
  IC1 = IC, DIP package, 16 pins [chip_label=AS3340]
  R3 = Resistor [tolerance=±5% resistance=470 package=THT]
  C1 = Film/Foil Capacitor [capacitance=100nF voltage=35V package="5mm [THT, pp]"]
  R6 = Resistor [tolerance=±5% resistance=1.8k package=THT]
  R7 = Resistor [tolerance=±5% resistance=1.5M package=THT]
  C2 = Film/Foil Capacitor [capacitance=100nF voltage=35V package="5mm [THT, pp]"]
  R8 = Resistor [tolerance=±5% resistance=470 package=THT]
  C3 = Film/Foil Capacitor [capacitance=100nF voltage=35V package="5mm [THT, pp]"]
  R9 = Resistor [tolerance=±5% resistance=22k package=THT]
  R10 = TRIMPOT [package=trimpot_pth_s3_lock]
  R11 = Resistor [tolerance=±5% resistance=680 package=THT]
  R12 = Resistor [tolerance=±5% resistance=5.6k package=THT]
  R13 = Resistor [tolerance=±5% resistance=5.6k package=THT]
  C4 = Ceramic Capacitor [capacitance=100nF package="100 mil [THT, multilayer]"]
  C5 = Electrolytic Capacitor [capacitance=1µF package="100 mil [THT, electrolytic]"]
  C6 = Electrolytic Capacitor [capacitance=1µF package="100 mil [THT, electrolytic]"]
  R14 = TRIMPOT [package=trimpot_pth_s3_lock]
  C7 = Ceramic Capacitor [capacitance=100nF package="100 mil [THT, multilayer]"]
  R15 = Resistor [tolerance=±5% resistance=1M package=THT]
  R16 = Resistor [tolerance=±5% resistance=270k package=THT]
  C8 = Ceramic Capacitor [capacitance=100nF package="100 mil [THT, multilayer]"]
  R19 = Resistor [tolerance=±5% resistance=1M package=THT]
  C9 = Ceramic Capacitor [capacitance=100nF package="100 mil [THT, multilayer]"]
  R21 = TRIMPOT [package=trimpot_pth_s3_lock]
  R22 = Resistor [tolerance=±5% resistance=100k package=THT]
  R23 = Resistor [tolerance=±5% resistance=100k package=THT]
  R24 = Resistor [tolerance=±5% resistance=100k package=THT]
  IC2 = Dual Op-Amp [package=dip08]
  C10 = Ceramic Capacitor [capacitance=100nF package="100 mil [THT, multilayer]"]
  C11 = Ceramic Capacitor [capacitance=100nF package="100 mil [THT, multilayer]"]
  R25 = Resistor [tolerance=±5% resistance=15k package=THT]
  R26 = Rotary Potentiometer (Small) [maximum_resistance=100kΩ package=THT]
  R27 = Rotary Potentiometer (Small) [maximum_resistance=100kΩ package=THT]
  R28 = Resistor [tolerance=±5% resistance=12k package=THT]
  IC3 = Dual Op-Amp [package=dip08]
  R29 = TRIMPOT [package=trimpot_pth_s3_lock]
  C12 = Ceramic Capacitor [capacitance=100nF package="100 mil [THT, multilayer]"]
  C13 = Ceramic Capacitor [capacitance=100nF package="100 mil [THT, multilayer]"]
  R30 = Resistor [tolerance=±5% resistance=10k package=THT]
  R31 = Resistor [tolerance=±5% resistance=10k package=THT]
  R32 = Resistor [tolerance=±5% resistance=2k package=THT]
  R33 = Resistor [tolerance=±5% resistance=1.2k package=THT]
  IC4 = Dual Op-Amp [package=dip08]
  C14 = Ceramic Capacitor [capacitance=100nF package="100 mil [THT, multilayer]"]
  C15 = Ceramic Capacitor [capacitance=100nF package="100 mil [THT, multilayer]"]
  C16 = Film/Foil Capacitor [capacitance=100nF voltage=35V package="5mm [THT, pp]"]
  R34 = Resistor [tolerance=±5% resistance=100k package=THT]
  R35 = Resistor [tolerance=±5% resistance=100 package=THT]
  R36 = Resistor [tolerance=±5% resistance=10 package=THT]
  IC5 = Dual Op-Amp [package=dip08]
  R37 = Resistor [tolerance=±5% resistance=10k package=THT]
  R38 = Resistor [tolerance=±5% resistance=10k package=THT]
  R39 = Resistor [tolerance=±5% resistance=10k package=THT]
  R40 = Resistor [tolerance=±5% resistance=10k package=THT]
  R41 = Resistor [tolerance=±5% resistance=10k package=THT]
  C17 = Ceramic Capacitor [capacitance=100nF package="100 mil [THT, multilayer]"]
  C18 = Ceramic Capacitor [capacitance=100nF package="100 mil [THT, multilayer]"]
  R42 = Rotary Potentiometer (Small) [maximum_resistance=100kΩ package=THT]

nets:
  N1: IC1.pin1, R9.Pin_1
  N2: IC1.pin2, R12.Pin_1
  N3: IC1.pin3, R10.CCW, R10.WIPER, R11.Pin_0, R12.Pin_0
  N4: IC1.pin4, R13.Pin_0
  N5: IC1.pin5, R27.wiper
  N6: IC1.pin6, C7.0
  N7: IC1.pin7, R14.CW
  N8: IC1.pin9, C8.1
  N9: IC1.pin10, IC3.B_+IN
  N10: IC1.pin11, C2.+
  N11: IC1.pin12, C1.+, R6.Pin_0, C2.-, C3.-, R13.Pin_1, C4.1, C5.-, C6.+, R14.CCW, C10.1, C11.1, R26.leg2, R28.Pin_0, C12.1, C13.1, R31.Pin_0, R33.Pin_1, C14.1, C15.1, R34.Pin_1, R41.Pin_1, C17.1, C18.1, R42.leg2
  N12: IC1.pin13, R7.Pin_1, R8.Pin_0, R19.Pin_0
  N13: IC1.pin14, R6.Pin_1
  N14: IC1.pin15, R3.Pin_1, R15.Pin_0, R16.Pin_1, R22.Pin_1, R23.Pin_1, R24.Pin_1
  N15: IC1.pin16, R7.Pin_0, C4.0, C5.+, R21.WIPER, R21.CW, IC2.A_V+, C11.0, IC3.A_V+, R29.CCW, R29.WIPER, C12.0, IC4.A_V+, C14.0, IC5.A_V+, C18.0
  N16: R3.Pin_0, C1.-
  N17: R8.Pin_1, C3.+
  N18: R9.Pin_0, R10.CW
  N19: R11.Pin_1, C6.-, IC2.A_V-, C10.0, IC3.A_V-, C13.0, IC4.A_V-, C15.0, IC5.A_V-, C17.0
  N20: R14.WIPER, R15.Pin_1
  N21: R16.Pin_0, R21.CCW
  N22: R19.Pin_1, C9.0
  N23: R22.Pin_0, IC5.B_-IN, IC5.B_OUT
  N24: R23.Pin_0, R42.wiper
  N25: IC2.A_OUT, IC2.A_-IN, R27.leg2
  N26: IC2.A_+IN, R26.wiper
  N27: IC2.B_+IN, R25.Pin_0, R28.Pin_1, R37.Pin_0
  N28: IC2.B_-IN, IC2.B_OUT, R26.leg1
  N29: R25.Pin_1, R29.CW
  N30: IC3.A_OUT, IC3.A_-IN
  N31: IC3.A_+IN, R32.Pin_1, R33.Pin_0
  N32: IC3.B_-IN, R30.Pin_1, R31.Pin_1
  N33: IC3.B_OUT, R30.Pin_0
  N34: IC4.A_OUT, IC4.A_-IN, C16.-
  N35: IC4.A_+IN, R36.Pin_0
  N36: IC4.B_+IN, C16.+, R34.Pin_0
  N37: IC4.B_-IN, IC4.B_OUT, R35.Pin_1
  N38: IC5.A_OUT, IC5.A_-IN, R42.leg1
  N39: IC5.A_+IN, R40.Pin_1, R41.Pin_0
  N40: R37.Pin_1, R39.Pin_0
  N41: R38.Pin_0, R39.Pin_1
  N42: R38.Pin_1, R40.Pin_0

notes:
  CV
  Triangle
  Pulse
  Saw
  GND
  +12V
  -12V
  GND
  PWM
  0-5V
  AS3340
  1 Scale1 16 VCC
  2 Scale2 15 VFCI
  3 VEE 14 Scale
  4 VP 13 VLFI
  5 VPWM 12 GND
  6 VHSI 11 Cap
  7 VHFT 10 VTO
  8 VSO 9 VSSI
  Hard
  Sync
  Soft Sync
  LIN FM
  Pulse
  Width
  Buffer
  In
  OUT_AC
  OUT
  Octave
  Fine
